// Digital circuit CPU.dig as structural Verilog
module CPU (
  input  [3:0] Select,
  input  Pulse,
  input  [15:0] ImmediateValue
);

  wire alu_1_carry, alu_1_equal, alu_1_greater, alu_1_less, alu_1_notequal, clock_1_clock_1, clock_1_clock_2,
       clock_1_clock_3, clock_1_clock_4, clock_1_clock_5, controlunit_1_d_alu_increment,
       controlunit_1_d_clk_cirfirst, controlunit_1_d_clk_cirsecond, controlunit_1_d_clk_flags,
       controlunit_1_d_clk_mdr, controlunit_1_d_clk_regbufferfirst, controlunit_1_d_clk_regbuffersecond,
       controlunit_1_d_clk_regoutput, controlunit_1_d_clk_rpc, controlunit_1_d_clk_sram,
       controlunit_1_d_rpc_memadder, controlunit_1_d_rpc_registers, controlunit_1_s_adr_direct,
       controlunit_1_s_adr_immediate, controlunit_1_s_alu_carryout, controlunit_1_s_alu_invert,
       controlunit_1_s_alu_orout, controlunit_1_s_alu_propagate, controlunit_1_s_alu_resultout,
       controlunit_1_s_ctl_halt, controlunit_1_s_mdr_writealu, controlunit_1_s_mdr_writemem,
       controlunit_1_s_mem_store, controlunit_1_s_reg_writealu, controlunit_1_s_reg_writemdr,
       flags_1_carry_out, flags_1_equal_out, flags_1_greater_out, flags_1_less_out, flags_1_notequal_out;
  wire [7:0] buffer_1_r1_out, buffer_1_r2_out, buffer_2_r1_out, buffer_2_r2_out, eeprom_1_data_out,
       mdr_1_data_out, registers_1_p4, registers_1_p6, sram_1_data_out;
  wire [15:0] addressor_1_data_out, memoryadder_1_data_out, rpc_1_data_out;

  RPC rpc_1 (
    .Reg_in(addressor_1_data_out), .Clk_write(controlunit_1_d_clk_rpc), .Add_in(memoryadder_1_data_out),
    .Reg_write(controlunit_1_d_rpc_registers), .Add_write(controlunit_1_d_rpc_memadder),
    .Data_out(rpc_1_data_out));
  MemoryAdder memoryadder_1 (.Data_in(rpc_1_data_out), .Data_out(memoryadder_1_data_out));
  EEPROM eeprom_1 (.Address_in(rpc_1_data_out), .Data_out(eeprom_1_data_out));
  Buffer buffer_1 (
    .R1_out(buffer_1_r1_out), .R2_out(buffer_1_r2_out), .Data_in(eeprom_1_data_out),
    .Clk_R1_write(controlunit_1_d_clk_cirfirst), .Clk_R2_write(controlunit_1_d_clk_cirsecond));
  Clock clock_1 (
    .Halt(controlunit_1_s_ctl_halt), .Pulse(Pulse), .Clock_1(clock_1_clock_1), .Clock_2(clock_1_clock_2),
    .Clock_3(clock_1_clock_3), .Clock_4(clock_1_clock_4), .Clock_5(clock_1_clock_5));  // open: Clock_6, Clock_7, Clock_8
  ControlUnit controlunit_1 (
    .FirstByte(buffer_1_r1_out), .SecondByte(buffer_1_r2_out), .Clock_1(clock_1_clock_1),
    .Clock_2(clock_1_clock_2), .Clock_3(clock_1_clock_3), .Clock_4(clock_1_clock_4),
    .Clock_5(clock_1_clock_5), .S_CTL_Halt(controlunit_1_s_ctl_halt),
    .S_ADR_Direct(controlunit_1_s_adr_direct), .S_ADR_Immediate(controlunit_1_s_adr_immediate),
    .S_ALU_OrOut(controlunit_1_s_alu_orout), .S_ALU_ResultOut(controlunit_1_s_alu_resultout),
    .S_ALU_Propagate(controlunit_1_s_alu_propagate), .S_ALU_Invert(controlunit_1_s_alu_invert),
    .S_ALU_CarryOut(controlunit_1_s_alu_carryout), .S_MDR_WriteMEM(controlunit_1_s_mdr_writemem),
    .S_MDR_WriteALU(controlunit_1_s_mdr_writealu), .S_MEM_Store(controlunit_1_s_mem_store),
    .S_REG_WriteMDR(controlunit_1_s_reg_writemdr), .S_REG_WriteALU(controlunit_1_s_reg_writealu),
    .D_Clk_MDR(controlunit_1_d_clk_mdr), .D_Clk_SRAM(controlunit_1_d_clk_sram),
    .D_Clk_RegOutput(controlunit_1_d_clk_regoutput),
    .D_Clk_RegBufferSecond(controlunit_1_d_clk_regbuffersecond),
    .D_Clk_RegBufferFirst(controlunit_1_d_clk_regbufferfirst), .D_Clk_Flags(controlunit_1_d_clk_flags),
    .D_Clk_RPC(controlunit_1_d_clk_rpc), .D_Clk_CIRSecond(controlunit_1_d_clk_cirsecond),
    .D_Clk_CIRFirst(controlunit_1_d_clk_cirfirst), .D_RPC_Registers(controlunit_1_d_rpc_registers),
    .D_RPC_MemAdder(controlunit_1_d_rpc_memadder), .D_ALU_Increment(controlunit_1_d_alu_increment),
    .F_NotEqual(flags_1_notequal_out), .F_Equal(flags_1_equal_out), .F_Less(flags_1_less_out),
    .F_Greater(flags_1_greater_out), .Carry(flags_1_carry_out));
  SRAM sram_1 (
    .Address_in(addressor_1_data_out), .Store(controlunit_1_s_mem_store),
    .Clk_write(controlunit_1_d_clk_sram), .Data_out(sram_1_data_out), .Data_in(mdr_1_data_out));
  MDR mdr_1 (
    .Data_mem(sram_1_data_out), .Clk_write(controlunit_1_d_clk_mdr), .Data_out(mdr_1_data_out),
    .Data_reg(registers_1_p4), .Write_mem(controlunit_1_s_mdr_writemem),
    .Write_reg(controlunit_1_s_mdr_writealu));
  // Registers registers_1: pin names not known; wires that end beside it: controlunit_1_s_reg_writemdr, controlunit_1_s_reg_writealu, mdr_1_data_out, registers_1_p4, controlunit_1_d_clk_regoutput, registers_1_p6, Select
  Buffer buffer_2 (
    .R1_out(buffer_2_r1_out), .R2_out(buffer_2_r2_out), .Data_in(registers_1_p6),
    .Clk_R1_write(controlunit_1_d_clk_regbufferfirst), .Clk_R2_write(controlunit_1_d_clk_regbuffersecond));
  Addressor addressor_1 (
    .Data_direct1(buffer_2_r1_out), .Data_imm(ImmediateValue), .Data_out(addressor_1_data_out),
    .Enable_direct(controlunit_1_s_adr_direct), .Enable_imm(controlunit_1_s_adr_immediate),
    .Data_direct2(buffer_2_r2_out));
  ALU alu_1 (
    .Data_2_in(buffer_2_r2_out), .Data_1_in(buffer_2_r1_out), .Data_out(registers_1_p4), .Carry(alu_1_carry),
    .Invert(controlunit_1_s_alu_invert), .Increment(controlunit_1_d_alu_increment), .Equal(alu_1_equal),
    .Greater(alu_1_greater), .Less(alu_1_less), .Out_carry(controlunit_1_s_alu_carryout),
    .Propagate(controlunit_1_s_alu_propagate), .Out_or(controlunit_1_s_alu_orout),
    .Out_result(controlunit_1_s_alu_resultout), .NotEqual(alu_1_notequal));
  Flags flags_1 (
    .Less_out(flags_1_less_out), .Less_in(alu_1_less), .Greater_in(alu_1_greater), .Equal_in(alu_1_equal),
    .Carry_in(alu_1_carry), .Greater_out(flags_1_greater_out), .Equal_out(flags_1_equal_out),
    .Carry_out(flags_1_carry_out), .Clock(controlunit_1_d_clk_flags), .NotEqual_out(flags_1_notequal_out),
    .NotEqual_in(alu_1_notequal));

  // Notes on the sheet:
  //   TICK 1
  //   -> First byte of instruction fetched
  //   -> Program counter incremented
  //   TICK 2
  //   -> Second byte of instruction fetched
  //   TICK 3
  //   -> First register fetched
  //   -> Program counter incremented
  //   TICK 4
  //   -> Second register fetched
  //   TICK 5
  //   -> Flag register written to
  //   -> Output register written to
  //   -> Program counter written to
  //   -> Memory written to
endmodule
