// Digital circuit CPU.dig as structural Verilog
module CPU (
);

  wire decoder_1_isopcodenibble, undriven;
  wire [3:0] undriven_2, undriven_3;
  wire [7:0] decoder_1_counter;
  wire [11:0] mem_adder_1_data_out, rpc_1_address;

  MEM_Adder mem_adder_1 (.Data_in(rpc_1_address), .Data_out(mem_adder_1_data_out));
  RPC rpc_1 (.Add_in(mem_adder_1_data_out), .Address(rpc_1_address));  // open: Reg_in
  Clock clock_1 (.S_CTL_HLT(undriven));
  EEPROM eeprom_1 ();  // open: Address, Data
  Decoder decoder_1 (.Nibble_1(undriven_3), .IsOpcodeNibble(decoder_1_isopcodenibble), .Counter(decoder_1_counter));
  SCU scu_1 (.Nibble_2(undriven_2), .IsOpcodeNibble(decoder_1_isopcodenibble), .Counter(decoder_1_counter));
endmodule
