// Digital circuit Clock.dig as structural Verilog
module Clock (
  input  Pulse,
  input  Halt,
  output Clock_1,
  output Clock_2,
  output Clock_3,
  output Clock_4,
  output Clock_5,
  output Clock_6,
  output Clock_7,
  output Clock_8
);

  wire not_1_out, not_2_out, or_1_out, or_2_out, or_3_out;
  wire [7:7] and_1_out;

  not not_1 (not_1_out, or_1_out);
  and and_1 (and_1_out[7], not_1_out, not_2_out);
  not not_2 (not_2_out, Halt);
  or or_1 (or_1_out, or_2_out, Clock_2, Clock_1);
  or or_2 (or_2_out, or_3_out, Clock_4, Clock_3);
  D_FF #(.Bits(8)) d_ff_1 (
    .D({and_1_out[7], Clock_1, Clock_2, Clock_3, Clock_4, Clock_5, Clock_6, Clock_7}), .C(Pulse),
    .Q({Clock_1, Clock_2, Clock_3, Clock_4, Clock_5, Clock_6, Clock_7, Clock_8}));  // open: nQ
  or or_3 (or_3_out, Clock_7, Clock_6, Clock_5);

  // Notes on the sheet:
  //   A CYCLE is composed of four TICKS
  //   A PULSE indicates that the cycle is moving to the next tick
  //   In a single cycle:
  //   [1] Clock_1 is set to high
  //   [2] Clock_1 is set to low
  //   [3] Clock_2 is set to high
  //   [4] Clock_2 is set to low
endmodule
