// Digital circuit ControlUnit.dig as structural Verilog
module ControlUnit (
  input  [7:0] FirstByte,
  input  [7:0] SecondByte,
  input  F_Greater,
  input  F_Less,
  input  F_Equal,
  input  F_NotEqual,
  input  Clock_5,
  input  Clock_4,
  input  Clock_3,
  input  Clock_2,
  input  Clock_1,
  input  Carry,
  output D_Clk_MDR,
  output D_Clk_SRAM,
  output D_Clk_RegOutput,
  output D_Clk_RegBufferSecond,
  output D_Clk_RegBufferFirst,
  output D_Clk_Flags,
  output D_Clk_RPC,
  output D_Clk_CIRSecond,
  output D_Clk_CIRFirst,
  output D_RPC_Registers,
  output D_RPC_MemAdder,
  output D_ALU_Increment,
  output S_CTL_Halt,
  output S_ADR_Direct,
  output S_ADR_Immediate,
  output S_ALU_OrOut,
  output S_ALU_ResultOut,
  output S_ALU_Propagate,
  output S_ALU_Invert,
  output S_ALU_CarryOut,
  output S_MEM_Store,
  output S_MDR_WriteMEM,
  output S_MDR_WriteALU,
  output S_REG_WriteMDR,
  output S_REG_WriteALU
);

  wire staticcontrolunit_1_nibble_2, staticcontrolunit_1_nibble_3, staticcontrolunit_1_s_alu_flagwrite,
       staticcontrolunit_1_s_alu_increment, staticcontrolunit_1_s_alu_usecarry,
       staticcontrolunit_1_s_bra_equal, staticcontrolunit_1_s_bra_greater, staticcontrolunit_1_s_bra_less,
       staticcontrolunit_1_s_bra_notequal, staticcontrolunit_1_s_bra_unconditional;

  StaticControlUnit staticcontrolunit_1 (
    .FirstByte(FirstByte), .SecondByte(SecondByte), .S_INS_ValReadCenter(S_CTL_Halt),
    .S_ALU_OrOut(S_ADR_Direct), .S_ALU_ResultOut(S_ADR_Immediate), .S_ALU_Propagate(S_ALU_OrOut),
    .S_ALU_Invert(S_ALU_ResultOut), .S_ALU_CarryOut(S_ALU_Propagate), .S_MDR_WriteMEM(S_ALU_Invert),
    .S_MDR_WriteALU(S_ALU_CarryOut), .S_MEM_Store(S_MDR_WriteMEM), .S_REG_WriteMDR(S_MDR_WriteALU),
    .S_REG_WriteALU(S_MEM_Store), .S_INS_RegReadSecond(S_REG_WriteMDR), .S_INS_RegReadFirst(S_REG_WriteALU),
    .S_ALU_FlagWrite(staticcontrolunit_1_s_alu_flagwrite),
    .S_BRA_NotEqual(staticcontrolunit_1_s_bra_notequal), .S_BRA_Equal(staticcontrolunit_1_s_bra_equal),
    .S_BRA_Less(staticcontrolunit_1_s_bra_less), .S_BRA_Greater(staticcontrolunit_1_s_bra_greater),
    .S_BRA_Unconditional(staticcontrolunit_1_s_bra_unconditional),
    .S_ALU_UseCarry(staticcontrolunit_1_s_alu_usecarry),
    .S_ALU_Increment(staticcontrolunit_1_s_alu_increment), .Nibble_2(staticcontrolunit_1_nibble_2),
    .Nibble_3(staticcontrolunit_1_nibble_3));  // open: S_CTL_Halt, S_INS_ValReadEnd, S_ADR_Direct, S_ADR_Immediate, Nibble_4
  SignalIntegrator signalintegrator_1 (
    .D_ALU_Increment(D_ALU_Increment), .D_RPC_MemAdder(D_RPC_MemAdder), .D_RPC_Registers(D_RPC_Registers),
    .D_CLK_CIRFirst(D_Clk_CIRFirst), .D_CLK_CIRSecond(D_Clk_CIRSecond), .D_CLK_RPC(D_Clk_RPC),
    .D_CLK_Flags(D_Clk_Flags), .D_CLK_RegBufferFirst(D_Clk_RegBufferFirst),
    .D_CLK_RegBufferSecond(D_Clk_RegBufferSecond), .D_CLK_RegOutput(D_Clk_RegOutput),
    .D_CLK_SRAM(D_Clk_SRAM), .D_CLK_MDR(D_Clk_MDR), .S_ALU_Increment(staticcontrolunit_1_nibble_3),
    .S_ALU_UseCarry(staticcontrolunit_1_nibble_2), .F_Carry(Carry),
    .S_BRA_Unconditional(staticcontrolunit_1_s_alu_increment),
    .S_BRA_Greater(staticcontrolunit_1_s_alu_usecarry), .F_Greater(F_Greater),
    .S_BRA_Less(staticcontrolunit_1_s_bra_unconditional), .F_Less(F_Less),
    .S_BRA_Equal(staticcontrolunit_1_s_bra_greater), .F_Equal(F_Equal),
    .S_BRA_NotEqual(staticcontrolunit_1_s_bra_less), .F_NotEqual(F_NotEqual),
    .S_ALU_FlagWrite(staticcontrolunit_1_s_bra_equal),
    .S_INS_RegReadFirst(staticcontrolunit_1_s_bra_notequal),
    .S_INS_RegReadSecond(staticcontrolunit_1_s_alu_flagwrite), .S_REG_WriteALU(S_REG_WriteALU),
    .S_REG_WriteMDR(S_REG_WriteMDR), .S_MEM_Store(S_MEM_Store), .S_MDR_WriteALU(S_MDR_WriteALU),
    .S_MDR_WriteMem(S_MDR_WriteMEM), .Clock_1(Clock_1), .Clock_2(Clock_2), .Clock_3(Clock_3),
    .Clock_4(Clock_4), .Clock_5(Clock_5));
endmodule
