// Digital circuit EEPROM.dig as structural Verilog
module EEPROM (
  input  [11:0] Address
);

  wire sram_1_d_0, sram_1_d_1, sram_1_d_2, sram_1_d_3, sram_1_d_4, sram_1_d_5, sram_1_d_6, sram_1_d_7;

  D_Flip_Flop d_flip_flop_1 (
    .VCC(1'b1), .GND(1'b0), ._1_D(sram_1_d_0), ._2_D(sram_1_d_1), ._3_D(sram_1_d_2), ._4_D(sram_1_d_3),
    ._5_D(sram_1_d_4), ._6_D(sram_1_d_5), ._7_D(sram_1_d_6), ._8_D(sram_1_d_7));  // open: EN, _1_Q, _3_Q, CLK, _2_Q, _4_Q, _5_Q, _7_Q, _6_Q, _8_Q
  D_Flip_Flop d_flip_flop_2 (
    .VCC(1'b1), .GND(1'b0), ._1_D(sram_1_d_0), ._2_D(sram_1_d_1), ._3_D(sram_1_d_2), ._4_D(sram_1_d_3),
    ._5_D(sram_1_d_4), ._6_D(sram_1_d_5), ._7_D(sram_1_d_6), ._8_D(sram_1_d_7));  // open: EN, _1_Q, _3_Q, CLK, _2_Q, _4_Q, _5_Q, _7_Q, _6_Q, _8_Q
  SRAM sram_1 (
    .NC(1'b0), .A_0(Address[0]), .A_1(Address[1]), .A_2(Address[2]), .A_3(Address[3]), .A_4(Address[4]),
    .A_5(Address[5]), .A_6(Address[6]), .A_7(Address[7]), .A_8(Address[8]), .A_9(Address[9]),
    .A_10(Address[10]), .A_11(Address[11]), .OE(1'b0), .GND(1'b0), .VCC(1'b1), .WE(1'b1), .A_12(1'b0),
    .CS_2(1'b1), .CS_1(1'b0), .D_0(sram_1_d_0), .D_1(sram_1_d_1), .D_2(sram_1_d_2), .D_3(sram_1_d_3),
    .D_4(sram_1_d_4), .D_5(sram_1_d_5), .D_6(sram_1_d_6), .D_7(sram_1_d_7));
endmodule
