// Digital circuit OperandIntegrator.dig as structural Verilog
module OperandIntegrator (
  input  [3:0] Nibble_1,
  input  [3:0] Nibble_2,
  input  [3:0] Nibble_3,
  input  S_INS_RegReadFirst,
  input  S_INS_RegReadSecond,
  input  S_INS_ValReadCenter,
  input  S_INS_ValReadEnd,
  output [7:0] Select,
  output [15:0] Value
);

  wire [3:1] undriven;

  Driver driver_1 (.in(Nibble_1[0]), .out(Value[0]));  // open: en
  // Pins of 1 and 4 bits meet at Nibble_1
  // Pins of 1 and 16 bits meet at Value
  // Pins of 1 and 4 bits meet at Nibble_2
  // Pins of 1 and 4 bits meet at Nibble_3
  // Pins of 1 and 16 bits meet at {undriven, 1'b0, Nibble_3, Nibble_2, Nibble_1}
  // Pins of 1 and 4 bits meet at {undriven, 1'b0}
endmodule
