// Digital circuit SCU.dig as structural Verilog
module SCU (
  input  [3:0] Nibble_2,
  input  IsOpcodeNibble,
  input  [7:0] Counter,
  output ALU_UseCarry,
  output ALU_Increment,
  output ALU_Invert,
  output ALU_Propagate,
  output ALU_ResultOut,
  output ALU_FlagWrite,
  output INS_RegReadSecond,
  output INS_RegReadFirst,
  output REG_WriteALU,
  output ALU_ResultOut_2
);

  wire not_1_1_1__1_y, not_1_1_1__2_y, or_2_1_1__1_y, or_2_1_1__2_y, or_2_1_1__3_y, or_2_1_1__4_y,
       or_2_1_2__1_y, or_2_1_2__2_y, or_2_1_2__3_y, or_2_1_2__4_y;

  LED _4_5 (.in(or_2_1_2__1_y));
  OR_2_1 or_2_1_1 (
    ._1_A(Counter[1]), ._1_Y(or_2_1_1__1_y), .VCC(1'b1), .GND(1'b0), ._1_B(Counter[3]), ._2_A(Counter[2]),
    ._2_Y(or_2_1_1__2_y), ._2_B(Counter[3]), ._3_B(Counter[6]), ._3_Y(or_2_1_1__3_y), ._3_A(or_2_1_1__2_y),
    ._4_B(Counter[4]), ._4_Y(or_2_1_1__4_y), ._4_A(or_2_1_1__3_y));
  OR_2_1 or_2_1_2 (
    ._1_A(Counter[4]), ._1_Y(or_2_1_2__1_y), .VCC(1'b1), .GND(1'b0), ._1_B(Counter[5]), ._2_A(Counter[0]),
    ._2_Y(or_2_1_2__2_y), ._2_B(Counter[3]), ._3_Y(or_2_1_2__3_y), ._4_B(or_2_1_1__3_y),
    ._4_Y(or_2_1_2__4_y), ._4_A(Counter[5]));  // open: _3_B, _3_A
  NOT_1_1 not_1_1_1 (
    ._1_A(Counter[6]), ._1_Y(not_1_1_1__1_y), ._2_A(or_2_1_2__1_y), ._2_Y(not_1_1_1__2_y), ._3_A(1'b0),
    ._4_A(1'b0), .VCC(1'b1), .GND(1'b0), ._5_A(1'b0), ._6_A(1'b0));  // open: _3_Y, _4_Y, _5_Y, _6_Y
  LED _2_3_6 (.in(or_2_1_1__3_y));
  AND_2_1 and_2_1_1 (
    ._1_A(or_2_1_1__1_y), ._1_Y(ALU_UseCarry), .VCC(1'b1), .GND(1'b0), ._1_B(Nibble_2[3]),
    ._2_A(or_2_1_1__4_y), ._2_Y(ALU_Increment), ._2_B(Nibble_2[3]), ._3_B(Nibble_2[3]), ._3_Y(ALU_Invert),
    ._3_A(or_2_1_2__4_y), ._4_B(Nibble_2[3]), ._4_Y(INS_RegReadSecond), ._4_A(not_1_1_1__1_y));
  AND_2_1 and_2_1_2 (
    ._1_A(not_1_1_1__2_y), ._1_Y(INS_RegReadFirst), .VCC(1'b1), .GND(1'b0), ._1_B(Nibble_2[3]),
    ._2_A(or_2_1_2__3_y), ._2_B(Nibble_2[2]), ._3_B(or_2_1_2__2_y), ._3_Y(ALU_ResultOut_2), ._3_A(Nibble_2[2]));  // open: _2_Y, _4_B, _4_Y, _4_A

  assign ALU_FlagWrite = Nibble_2[3];
  assign ALU_Propagate = Nibble_2[3];
  assign ALU_ResultOut = Nibble_2[3];
  assign REG_WriteALU = Nibble_2[3];

  // Notes on the sheet:
  //   Nibble_2: pin 2
  //   IsOpcodeNibble: pin 40
  //   Counter: pin 1
endmodule
