// Digital circuit Nibble Combinator.dig as structural Verilog
module Nibble_Combinator (
  input  [7:0] Counter,
  input  Active,
  output ADR_Immediate,
  output INS_ValRead,
  output MEM_Store,
  output MDR_WriteMem,
  output REG_WriteVal
);

  wire not_1_out;

  not not_1 (not_1_out, Counter[7]);
  and and_1 (ADR_Immediate, not_1_out, Active);
  and and_2 (MEM_Store, Counter[1], Active);
  and and_3 (MDR_WriteMem, Counter[0], Active);
  and and_4 (REG_WriteVal, Counter[7], Active);

  assign INS_ValRead = Active;
endmodule
