// Digital circuit MemoryAdder.dig as structural Verilog
module MemoryAdder (
  input  [15:0] Data_in,
  output [15:0] Data_out
);

  wire [15:0] and_1_out, and_2_out, xor_1_out;
  wire [15:1] or_1_out;
  wire [15:15] or_1_out_2;

  assign xor_1_out = Data_in ^ 16'h1;  // XOr xor_1, 16 bits wide
  assign and_1_out = 16'h1 & Data_in;  // And and_1, 16 bits wide
  assign Data_out = xor_1_out ^ {or_1_out, 1'b0};  // XOr xor_2, 16 bits wide
  assign and_2_out = xor_1_out & {or_1_out, 1'b0};  // And and_2, 16 bits wide
  assign {or_1_out_2[15], or_1_out} = and_2_out | and_1_out;  // Or or_1, 16 bits wide

  // Notes on the sheet:
  //   Data_in: pin 1
  //   Data_out: pin 12
  //   Data_out = Data_in + 1
endmodule

/* Test case:
	     Data_in Data_out
loop(a, 1024)
	(a) (a+1)
end loop
*/
