// Digital circuit Flags.dig as structural Verilog
module Flags (
  input  Less_in,
  input  Greater_in,
  input  Equal_in,
  input  Carry_in,
  input  Clock,
  output Less_out,
  output Greater_out,
  output Equal_out,
  output Carry_out
);

  D_FF #(.Bits(4)) d_ff_1 (
    .D({Carry_in, Equal_in, Greater_in, Less_in}), .C(Clock),
    .Q({Carry_out, Equal_out, Greater_out, Less_out}));  // open: nQ

  // Notes on the sheet:
  //   Less_out: pin 9
  //   Greater_out: pin 8
  //   Equal_out: pin 7
  //   Carry_out: pin 6
  //   Clock: pin 1
endmodule
